# Fritzing sketch connections (saved by Fritzing 0.9.3b)

parts:
  L298N1 = L298N DC motor driver
  Part1 = Arduino Mega ADK (Rev3)
  DC_Mot_Enc1 = DC Motor with two-phase hall-encoder [part_number=VT-E-G25A-06-177E]
  DC_Mot_Enc2 = DC Motor with two-phase hall-encoder [part_number=VT-E-G25A-06-177E]
  VCC1 = 4 x AAA Battery Mount  # not connected

nets:
  N1: L298N1.OUT1, DC_Mot_Enc1.pin6
  N2: L298N1.OUT2, DC_Mot_Enc1.pin1
  N3: L298N1.OUT3, DC_Mot_Enc2.pin1
  N4: L298N1.OUT4, DC_Mot_Enc2.pin6
  N5: L298N1.5V#9, L298N1.ENA
  N6: L298N1.5V#10, L298N1.ENB
  N7: L298N1.IN1, Part1.D9_PWM
  N8: L298N1.IN2, Part1.D8_PWM
  N9: L298N1.IN3, Part1.D11_PWM
  N10: L298N1.IN4, Part1.D10_PWM
  N11: Part1.D21/SCL, DC_Mot_Enc2.pin3
  N12: Part1.D20/SDA, DC_Mot_Enc2.pin4
  N13: Part1.D19/RX1, DC_Mot_Enc1.pin3
  N14: Part1.D18/TX1, DC_Mot_Enc1.pin4
  N15: Part1.IOREF, Part1.5V, DC_Mot_Enc1.pin2, DC_Mot_Enc2.pin2
  N16: Part1.GND, DC_Mot_Enc1.pin5, DC_Mot_Enc2.pin5

custom parts:
  L298N DC motor driver: 2x DC motor driver with 78M05 positive voltage regulator (7..35 V) L298N: max 46 V, 2 A Set 5 V Enable jumper to enable 5 V regultor (needed for the L298N) and +5 V output at screw terminal or supply external +5 V at screw terminal Set ENA and/or ENB to +5 V to enable motor permanently or supply ENA and/or ENB with PWM signal IN1 and IN2 set rotation directory for motor A (OUT1/OUT2) IN2 and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
